# Fritzing sketch smart-parking-rangkaian-arduino-nano-2 (saved by Fritzing 0.9.3b)
breadboards: 1

parts:
  Part1 = Arduino Nano (Rev3.0)
  LED1 = smd LED [color="Red (633nm)" package="0805 [SMD]"]
  LED2 = smd LED [color="Yellow (574nm)" package="0805 [SMD]"]
  LED3 = smd LED [color="Green (555nm)" package="0805 [SMD]"]
  HC-SR04_Sensor_1 = HC-SR04 Ultrasonic Distance Sensor
  R1 = Resistor [tolerance=±5% resistance=220 package="2512 [SMD]"]
  J1 = Buzzer

nets:
  GND: Part1.GND, HC-SR04_Sensor_1.GND, R1.Pin_0, J1.pin1
  N1: Part1.D2, HC-SR04_Sensor_1.TRIG
  N2: Part1.D3, HC-SR04_Sensor_1.ECHO
  N3: Part1.D5, J1.pin2
  N4: Part1.D6, LED3.anode
  N5: Part1.D9, LED2.anode
  N6: Part1.D11/MOSI, LED1.anode
  5V: Part1.5V, HC-SR04_Sensor_1.VCC
  N7: LED1.cathode, LED2.cathode, LED3.cathode

custom parts:
  Buzzer: Fixed frequency buzzer
