# Fritzing sketch smart-parking-rangkaian-arduino-nano (saved by Fritzing 0.9.3b)
circuit board: 8.46667cm x 5.64444cm
breadboards: 1

parts:
  Part2 = Arduino Nano (Rev3.0) (ICSP)
  HC-SR04_Sensor_1 = HC-SR04 Ultrasonic Distance Sensor
  J1 = Buzzer
  LED1 = LED - 5mm [color="Red (633nm)" package="5 mm [THT]"]
  LED2 = LED - 5mm [color="Yellow (595nm)" package="5 mm [THT]"]
  LED3 = LED - 5mm [color="Green (560nm)" package="5 mm [THT]"]
  R1 = Resistor [tolerance=±5% resistance=100 package="1206 [SMD]"]

nets:
  GND: Part2.GND, HC-SR04_Sensor_1.GND, J1.pin1, R1.Pin_0
  N1: Part2.D2, HC-SR04_Sensor_1.TRIG
  N2: Part2.D3, HC-SR04_Sensor_1.ECHO
  N3: Part2.D5, J1.pin2
  N4: Part2.D6, LED3.anode
  N5: Part2.D9, LED2.anode
  5V: Part2.5V, HC-SR04_Sensor_1.VCC
  N6: LED1.cathode, LED2.cathode, LED3.cathode, R1.Pin_1

custom parts:
  Buzzer: Fixed frequency buzzer
